// Logisim project IT012_LAB1_25520339.circ as structural Verilog: 5 circuits, main circuit TN1
module TN1 (
  input  C,
  input  A,
  input  B,
  output CHAIN,
  output NAND3,
  output XNOR3,
  output A_prime,
  output AND,
  output OR,
  output NAND,
  output NOR,
  output XOR,
  output XNOR
);

  wire nand_3_out;

  nand nand_1 (NAND3, C, A, B);
  xor xor_1 (XNOR3, C, A, B);
  not not_1 (A_prime, A);
  and and_1 (AND, A, B);
  or or_1 (OR, A, B);
  nand nand_2 (NAND, A, B);
  nor nor_1 (NOR, A, B);
  xor xor_2 (XOR, A, B);
  xnor xnor_1 (XNOR, A, B);
  nand nand_3 (nand_3_out, C, NAND);
  nand nand_4 (CHAIN, nand_3_out, NAND);
endmodule

module TN2 (
  input  X,
  input  Y,
  input  Z,
  output EQ5,
  output EQ4,
  output EQ1,
  output EQ2,
  output EQ3
);

  wire and_1_out, and_2_out, and_3_out, and_4_out, and_5_out, nand_1_out, nor_1_out, or_1_out, or_2_out,
       or_3_out, or_4_out, or_5_out;

  or or_1 (or_1_out, X, Y);
  and and_1 (and_1_out, ~X, Y);  // AND_Gate
  nor nor_1 (nor_1_out, X, Y);
  and and_2 (and_2_out, ~X, ~Y);  // AND_Gate
  nand nand_1 (nand_1_out, X, Y);
  and and_3 (and_3_out, ~X, ~Y);  // AND_Gate
  and and_4 (and_4_out, Y, Z);
  or or_2 (or_2_out, X, Y);
  or or_3 (or_3_out, X, Z);
  or or_4 (or_4_out, X, and_1_out);
  xnor xnor_1 (EQ1, nor_1_out, and_2_out);
  xnor xnor_2 (EQ2, nand_1_out, and_3_out);
  or or_5 (or_5_out, and_4_out, X);
  and and_5 (and_5_out, or_2_out, or_3_out);
  xnor xnor_3 (EQ5, or_4_out, or_1_out);
  xnor xnor_4 (EQ4, X, or_4_out);
  xnor xnor_5 (EQ3, or_5_out, and_5_out);
endmodule

module TN3 (
  input  A,
  input  B,
  input  C,
  input  D,
  output F
);

  wire and_1_out, and_2_out, and_3_out, and_4_out, and_5_out, and_6_out, not_1_out, not_2_out, not_3_out,
       not_4_out;

  not not_1 (not_1_out, A);
  not not_2 (not_2_out, B);
  not not_3 (not_3_out, C);
  not not_4 (not_4_out, D);
  and and_1 (and_1_out, not_1_out, not_2_out, C, not_4_out);
  and and_2 (and_2_out, not_1_out, not_2_out, C, D);
  and and_3 (and_3_out, not_1_out, B, not_3_out, D);
  and and_4 (and_4_out, not_1_out, B, C, D);
  and and_5 (and_5_out, A, not_2_out, C, D);
  and and_6 (and_6_out, A, B, not_3_out, D);
  or or_1 (F, and_1_out, and_2_out, and_3_out, and_4_out, and_5_out, and_6_out);
endmodule

module TN4 (
  input  A,
  input  B,
  input  C,
  input  D,
  output F_can,
  output EQ1,
  output F_SoP,
  output EQ2,
  output F_PoS
);

  wire and_1_out, and_2_out, and_3_out, and_4_out, and_5_out, and_6_out, and_7_out, and_8_out, and_9_out,
       and_10_out, not_1_out, not_2_out, not_3_out, not_4_out, or_1_out, or_2_out, or_3_out, or_4_out,
       or_5_out;

  not not_1 (not_1_out, A);
  not not_2 (not_2_out, B);
  not not_3 (not_3_out, C);
  not not_4 (not_4_out, C);
  and and_1 (and_1_out, not_1_out, not_2_out, C, not_4_out);
  and and_2 (and_2_out, not_1_out, not_2_out, C, C);
  and and_3 (and_3_out, not_1_out, B, not_3_out, C);
  and and_4 (and_4_out, not_1_out, B, C, C);
  and and_5 (and_5_out, A, not_2_out, C, C);
  and and_6 (and_6_out, A, B, not_3_out, C);
  and and_7 (and_7_out, not_1_out, not_2_out, C);
  and and_8 (and_8_out, not_1_out, B, C);
  and and_9 (and_9_out, B, not_3_out, C);
  and and_10 (and_10_out, not_2_out, C, C);
  or or_1 (or_1_out, C, C);
  or or_2 (or_2_out, B, C, not_4_out);
  or or_3 (or_3_out, not_2_out, not_3_out, C);
  or or_4 (or_4_out, not_1_out, not_2_out, not_3_out);
  or or_5 (or_5_out, not_1_out, not_3_out, C);
  or or_6 (F_can, and_1_out, and_2_out, and_3_out, and_4_out, and_5_out, and_6_out);
  or or_7 (F_SoP, and_7_out, and_8_out, and_9_out, and_10_out);
  and and_11 (F_PoS, or_1_out, or_2_out, or_3_out, or_4_out, or_5_out);
  xnor xnor_1 (EQ1, F_can, F_SoP);
  xnor xnor_2 (EQ2, F_can, F_PoS);

  assign D = C;
endmodule

module TN5 (
  input  A,
  input  B,
  input  C,
  output F
);

  wire xor_1_out;

  xor xor_1 (xor_1_out, A, B);
  xor xor_2 (F, xor_1_out, C);
endmodule
