// Logisim project IT012_Lab02_25520339.circ as structural Verilog: 8 circuits, main circuit warmup
module warmup (
  input  [7:0] A,
  input  [7:0] B,
  output [7:0] S
);

  Adder adder_1 (.a(A), .b(B), .out(S));  // open: cin, cout
  // Probe on S
endmodule

module FA (
  input  A,
  input  B,
  input  Cin,
  output S,
  output Cout
);

  wire and_1_out, and_2_out, xor_1_out;

  xor xor_1 (xor_1_out, A, B);
  and and_1 (and_1_out, xor_1_out, Cin);
  and and_2 (and_2_out, B, A);
  xor xor_2 (S, xor_1_out, Cin);
  or or_1 (Cout, and_1_out, and_2_out);
endmodule

module ADDSUB4 (
  input  [3:0] A,
  input  [3:0] B,
  input  SUB,
  output C1,
  output [3:0] S,
  output C2,
  output C3,
  output C
);

  FA fa_1 (.A(A[0]), .B(B[0]), .Cin(1'b0), .S(S[0]), .Cout(C1));
  FA fa_2 (.A(A[1]), .B(B[1]), .Cin(C1), .S(S[1]), .Cout(C2));
  FA fa_3 (.A(A[2]), .B(B[2]), .Cin(C2), .S(S[2]), .Cout(C3));
  FA fa_4 (.A(A[3]), .B(B[3]), .Cin(C3), .S(S[3]), .Cout(C));
endmodule

module ALU8 (
  input  [7:0] A,
  input  [7:0] B,
  input  [2:0] OP,
  output LT,
  output Z,
  output [7:0] R
);

  wire and_2_out, and_3_out, and_4_out, not_1_out;
  wire [7:0] adder_1_out, adder_2_out, and_1_out, multiplexer_1_out, multiplexer_2_out, not_2_out, or_1_out,
       subtractor_1_out, subtractor_2_out, xor_1_out;

  not not_1 (not_1_out, B[7]);
  Adder adder_1 (.a(A), .b(B), .out(adder_1_out));  // open: cin, cout
  Adder adder_2 (.a(A), .b(8'h1), .out(adder_2_out));  // open: cin, cout
  Subtractor subtractor_1 (.a(A), .b(B), .out(subtractor_1_out));  // open: bin, bout
  Subtractor subtractor_2 (.a(A), .b(8'h1), .out(subtractor_2_out));  // open: bin, bout
  assign and_1_out = A & B;  // AND_Gate and_1, 8 bits wide
  assign or_1_out = A | B;  // OR_Gate or_1, 8 bits wide
  assign not_2_out = ~A;  // NOT_Gate not_2, 8 bits wide
  assign xor_1_out = A ^ B;  // XOR_Gate xor_1, 8 bits wide
  and and_2 (and_2_out, A[7], not_1_out);
  and and_3 (and_3_out, A[7], R[7]);
  and and_4 (and_4_out, R[7], not_1_out);
  Multiplexer #(.select(2), .width(8), .enable("false")) multiplexer_1 (
    .in0(adder_1_out), .in1(adder_2_out), .in2(subtractor_1_out), .in3(subtractor_2_out),
    .out(multiplexer_1_out), .sel(OP[1:0]));
  Multiplexer #(.select(2), .width(8), .enable("false")) multiplexer_2 (
    .in0(and_1_out), .in1(or_1_out), .in2(not_2_out), .in3(xor_1_out), .out(multiplexer_2_out), .sel(OP[1:0]));
  or or_2 (LT, and_2_out, and_3_out, and_4_out);
  Multiplexer #(.width(8), .enable("false")) multiplexer_3 (
    .in0(multiplexer_1_out), .in1(multiplexer_2_out), .out(R), .sel(OP[2]));
  nor nor_1 (Z, R[0], R[1], R[2], R[3], R[4], R[5], R[6], R[7]);
endmodule

module DLATCH (
  input  D,
  input  E,
  output Q
);

  Multiplexer #(.enable("false")) multiplexer_1 (.in0(Q), .in1(D), .out(Q), .sel(E));
endmodule

module TN3 (
  input  D,
  input  CLK,
  input  D3_5,
  input  CLK3_5,
  output Q2,
  output Q1,
  output out_7,
  output out_8
);

  wire d_ff_2_q, dlatch_2_q;

  D_Flip_Flop d_ff_1 (.clk(CLK), .D(D), .Q(Q2));  // open: Qn, preset, en, reset
  DLATCH dlatch_1 (.D(D), .E(CLK), .Q(Q1));
  DLATCH dlatch_2 (.D(D3_5), .E(CLK3_5), .Q(dlatch_2_q));
  D_Flip_Flop d_ff_2 (.clk(CLK3_5), .D(D3_5), .Q(d_ff_2_q));  // open: Qn, preset, en, reset
  DLATCH dlatch_3 (.D(dlatch_2_q), .E(CLK3_5), .Q(out_7));
  D_Flip_Flop d_ff_3 (.clk(CLK3_5), .D(d_ff_2_q), .Q(out_8));  // open: Qn, preset, en, reset
endmodule

module REGFILE (
  input  WE,
  input  [1:0] RD,
  input  [1:0] RA,
  input  [7:0] DIN,
  input  CLK,
  input  [1:0] RB,
  output [7:0] QA,
  output [7:0] R0,
  output [7:0] R1,
  output [7:0] R2,
  output [7:0] R3,
  output [7:0] QB
);

  wire decoder_1_out0, decoder_1_out1, decoder_1_out2, decoder_1_out3;

  Decoder #(.select(2)) decoder_1 (
    .out0(decoder_1_out0), .out1(decoder_1_out1), .out2(decoder_1_out2), .out3(decoder_1_out3), .sel(RD),
    .en(WE));
  Register register_1 (.D(DIN), .en(decoder_1_out0), .Q(R0), .clk(CLK));  // open: clr
  Register register_2 (.D(DIN), .en(decoder_1_out1), .Q(R1), .clk(CLK));  // open: clr
  Register register_3 (.D(DIN), .en(decoder_1_out2), .Q(R2), .clk(CLK));  // open: clr
  Register register_4 (.D(DIN), .en(decoder_1_out3), .Q(R3), .clk(CLK));  // open: clr
  Multiplexer #(.select(2), .width(8), .enable("false")) multiplexer_1 (
    .in0(R0), .in1(R1), .in2(R2), .in3(R3), .out(QA), .sel(RA));
  Multiplexer #(.select(2), .width(8), .enable("false")) multiplexer_2 (
    .in0(R3), .in1(R2), .in2(R1), .in3(R0), .out(QB), .sel(RB));
endmodule

module DATAPATH (
  input  WE,
  input  [1:0] RD,
  input  CLK,
  input  [2:0] OP,
  input  [7:0] IMM,
  input  SRC,
  input  [1:0] RA,
  input  [1:0] RB,
  output [7:0] R0,
  output [7:0] R1,
  output [7:0] R2,
  output [7:0] R3,
  output Z,
  output [7:0] R
);

  wire [7:0] multiplexer_1_out, regfile_1_qa, regfile_1_qb;

  ALU8 alu8_1 (.A(regfile_1_qa), .B(regfile_1_qb), .OP(OP), .Z(Z), .R(R));  // open: LT
  Multiplexer #(.width(8), .enable("false")) multiplexer_1 (.in0(R), .in1(IMM), .out(multiplexer_1_out), .sel(SRC));
  REGFILE regfile_1 (
    .WE(WE), .RD(RD), .DIN(multiplexer_1_out), .CLK(CLK), .RA(RA), .RB(RB), .QA(regfile_1_qa), .R0(R0),
    .R1(R1), .R2(R2), .R3(R3), .QB(regfile_1_qb));
endmodule
